# Fritzing sketch A2 sketch (saved by Fritzing 0.9.3b)
breadboards: 1

parts:
  J1 = Basic Force Sensing Resistor (FSR) [package=THT]
  J2 = Basic Force Sensing Resistor (FSR) [package=THT]
  R1 = Resistor [tolerance=±5% resistance=220 package=THT]
  R2 = Resistor [tolerance=±5% resistance=220 package=THT]
  U1 = 74HC595 [package="DIP16 [THT]"]
  S1 = Pushbutton [package="[THT]"]
  R3 = Resistor [tolerance=±5% resistance=220 package=THT]
  Raspberry_Pi_Zero1 = Raspberry Pi B rev1

nets:
  N1: J1.pin_0, J2.pin_1, U1.Q1, U1.Q2, R3.Pin_1, Raspberry_Pi_Zero1.3V3
  N2: J1.pin_1, R1.Pin_0, U1.VCC
  N3: J2.pin_0, R2.Pin_0, U1.Q0
  GND: R1.Pin_1, R2.Pin_1, U1.Q3, U1.GND, S1.Pin_3, S1.Pin_4, Raspberry_Pi_Zero1.GND
  N4: U1.Q4, Raspberry_Pi_Zero1.GPIO_18
  N5: U1.Q5, Raspberry_Pi_Zero1.GPIO_23
  N6: U1.Q7, Raspberry_Pi_Zero1.GPIO_25
  N7: S1.Pin_1, S1.Pin_2, R3.Pin_0, Raspberry_Pi_Zero1.GPIO_10
